// Digital circuit mult.dig as structural Verilog
module mult (
  input  [15:0] A,
  input  [15:0] B,
  output [31:0] Q,
  output C,
  output [16:0] out_5,
  output [16:0] out_6,
  output [31:0] out_7,
  output [31:0] out_8,
  output [15:0] out_9
);

  assign out_9 = ~B;  // Not not_1, 16 bits wide
  Add #(.Bits(16)) A_plus_B (.a(A), .b(B), .c_i(1'b0), .s(out_5[15:0]), .c_o(out_5[16]));
  Add #(.Bits(16)) A_B (.a(A), .b(out_9), .c_i(1'b1), .s(out_6[15:0]), .c_o(out_6[16]));
  ROM #(.AddrBits(17), .Bits(32)) n_2_4 (.A(out_5), .sel(1'b1), .D(out_7));
  ROM #(.AddrBits(17), .Bits(32)) n_2_4_2 (.A(out_6), .sel(1'b1), .D(out_8));
  Add #(.Bits(32)) Q0_Q1 (.a(out_7), .b(out_8), .c_i(1'b1), .s(Q), .c_o(C));

  // Notes on the sheet:
  //   contents of n_2_4 (hex, n*v repeats v):
  //   0,0,1,2,4,6,9,c,10,14,19,1e,24,2a,31,38,40,48,51,5a,64,6e,79,84
  //   ,90,9c,a9,b6,c4,d2,e1,f0,100,110,121,132,144,156,169,17c,190,1a4
  //   ,1b9,1ce,1e4,1fa,211,228,240,258,271,28a,2a4,2be,2d9,2f4,310,32c
  //   ,349,366,384,3a2,3c1,3e0,400,420,441,462,484,4a6,4c9,4ec,510,534
  //   ,559,57e,5a4,5ca,5f1,618,640,668,691,6ba,6e4,70e,739,764,790,7bc
  //   ,7e9,816,844,872,8a1,8d0,900,930,961,992,9c4,9f6,a29,a5c,a90,ac4
  //   ,af9,b2e,b64,b9a,bd1,c08,c40,c78,cb1,cea,d24,d5e,d99,dd4,e10,e4c
  //   ,e89,ec6,f04,f42,f81,fc0,1000,1040,1081,10c2,1104,1146,1189,11cc
  //   ,1210,1254,1299,12de,1324,136a,13b1,13f8,1440,1488,14d1,151a,1564
  //   ,15ae,15f9,1644,1690,16dc,1729,1776,17c4,1812,1861,18b0,1900,1950
  //   ,19a1,19f2,1a44,1a96,1ae9,1b3c,1b90,1be4,1c39,1c8e,1ce4,1d3a,1d91
  //   ,1de8,1e40,1e98,1ef1,1f4a,1fa4,1ffe,2059,20b4,2110,216c,21c9,2226
  //   ,2284,22e2,2341,23a0,2400,2460,24c1,2522,2584,25e6,2649,26ac,2710
  //   ,2774,27d9,283e,28a4,290a,2971,29d8,2a40,2aa8,2b11,2b7a,2be4,2c4e
  //   ,2cb9,2d24,2d90,2dfc,2e69,2ed6,2f44,2fb2,3021,3090,3100,3170,31e1
  //   ,3252,32c4,3336,33a9,341c,3490,3504,3579,35ee,3664,36da,3751,37c8
  //   ,3840,38b8,3931,39aa,3a24,3a9e,3b19,3b94,3c10,3c8c,3d09,3d86,3e04
  //   ,3e82,3f01,3f80,4000,4080,4101,4182,4204,4286,4309,438c,4410,4494
  //   ,4519,459e,4624,46aa,4731,47b8,4840,48c8,4951,49da,4a64,4aee,4b79
  //   ,4c04,4c90,4d1c,4da9,4e36,4ec4,4f52,4fe1,5070,5100,5190,5221,52b2
  //   ,5344,53d6,5469,54fc,5590,5624,56b9,574e,57e4,587a,5911,59a8,5a40
  //   ,5ad8,5b71,5c0a,5ca4,5d3e,5dd9,5e74,5f10,5fac,6049,60e6,6184,6222
  //   ,62c1,6360,6400,64a0,6541,65e2,6684,6726,67c9,686c,6910,69b4,6a59
  //   ,6afe,6ba4,6c4a,6cf1,6d98,6e40,6ee8,6f91,703a,70e4,718e,7239,72e4
  //   ,7390,743c,74e9,7596,7644,76f2,77a1,7850,7900,79b0,7a61,7b12,7bc4
  //   ,7c76,7d29,7ddc,7e90,7f44,7ff9,80ae,8164,821a,82d1,8388,8440,84f8
  //   ,85b1,866a,8724,87de,8899,8954,8a10,8acc,8b89,8c46,8d04,8dc2,8e81
  //   ,8f40,9000,90c0,9181,9242,9304,93c6,9489,954c,9610,96d4,9799,985e
  //   ,9924,99ea,9ab1,9b78,9c40,9d08,9dd1,9e9a,9f64,a02e,a0f9,a1c4,a290
  //   ,a35c,a429,a4f6,a5c4,a692,a761,a830,a900,a9d0,aaa1,ab72,ac44,ad16
  //   ,ade9,aebc,af90,b064,b139,b20e,b2e4,b3ba,b491,b568,b640,b718,b7f1
  //   ,b8ca,b9a4,ba7e,bb59,bc34,bd10,bdec,bec9,bfa6,c084,c162,c241,c320
  //   ,c400,c4e0,c5c1,c6a2,c784,c866,c949,ca2c,cb10,cbf4,ccd9,cdbe,cea4
  //   ,cf8a,d071,d158,d240,d328,d411,d4fa,d5e4,d6ce,d7b9,d8a4,d990,da7c
  //   ,db69,dc56,dd44,de32,df21,e010,e100,e1f0,e2e1,e3d2,e4c4,e5b6,e6a9
  //   ,e79c,e890,e984,ea79,eb6e,ec64,ed5a,ee51,ef48,f040,f138,f231,f32a
  //   ,f424,f51e,f619,f714,f810,f90c,fa09,fb06,fc04,fd02,fe01,ff00,10000
  //   ,10100,10201,10302,10404,10506,10609,1070c,10810,10914,10a19,10b1e
  //   ,10c24,10d2a,10e31,10f38,11040,11148,11251,1135a,11464,1156e,11679
  //   ,11784,11890,1199c,11aa9,11bb6,11cc4,11dd2,11ee1,11ff0,12100,12210
  //   ,12321,12432,12544,12656,12769,1287c,12990,12aa4,12bb9,12cce,12de4
  //   ,12efa,13011,13128,13240,13358,13471,1358a,136a4,137be,138d9,139f4
  //   ,13b10,13c2c,13d49,13e66,13f84,140a2,141c1,142e0,14400,14520,14641
  //   ,14762,14884,149a6,14ac9,14bec,14d10,14e34,14f59,1507e,151a4,152ca
  //   ,153f1,15518,15640,15768,15891,159ba,15ae4,15c0e,15d39,15e64,15f90
  //   ,160bc,161e9,16316,16444,16572,166a1,167d0,16900,16a30,16b61,16c92
  //   ,16dc4,16ef6,17029,1715c,17290,173c4,174f9,1762e,17764,1789a,179d1
  //   ,17b08,17c40,17d78,17eb1,17fea,18124,1825e,18399,184d4,18610,1874c
  //   ,18889,189c6,18b04,18c42,18d81,18ec0,19000,19140,19281,193c2,19504
  //   ,19646,19789,198cc,19a10,19b54,19c99,19dde,19f24,1a06a,1a1b1,1a2f8
  //   ,1a440,1a588,1a6d1,1a81a,1a964,1aaae,1abf9,1ad44,1ae90,1afdc,1b129
  //   ,1b276,1b3c4,1b512,1b661,1b7b0,1b900,1ba50,1bba1,1bcf2,1be44,1bf96
  //   ,1c0e9,1c23c,1c390,1c4e4,1c639,1c78e,1c8e4,1ca3a,1cb91,1cce8,1ce40
  //   ,1cf98,1d0f1,1d24a,1d3a4,1d4fe,1d659,1d7b4,1d910,1da6c,1dbc9,1dd26
  //   ,1de84,1dfe2,1e141,1e2a0,1e400,1e560,1e6c1,1e822,1e984,1eae6,1ec49
  //   ,1edac,1ef10,1f074,1f1d9,1f33e,1f4a4,1f60a,1f771,1f8d8,1fa40,1fba8
  //   ,1fd11,1fe7a,1ffe4,2014e,202b9,20424,20590,206fc,20869,209d6,20b44
  //   ,20cb2,20e21,20f90,21100,21270,213e1,21552,216c4,21836,219a9,21b1c
  //   ,21c90,21e04,21f79,220ee,22264,223da,22551,226c8,22840,229b8,22b31
  //   ,22caa,22e24,22f9e,23119,23294,23410,2358c,23709,23886,23a04,23b82
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  //   contents of n_2_4_2 (hex, n*v repeats v):
  //   bfffffff,c0007fff,c000fffe,c0017ffd,c001fffb,c0027ff9,c002fff6
  //   ,c0037ff3,c003ffef,c0047feb,c004ffe6,c0057fe1,c005ffdb,c0067fd5
  //   ,c006ffce,c0077fc7,c007ffbf,c0087fb7,c008ffae,c0097fa5,c009ff9b
  //   ,c00a7f91,c00aff86,c00b7f7b,c00bff6f,c00c7f63,c00cff56,c00d7f49
  //   ,c00dff3b,c00e7f2d,c00eff1e,c00f7f0f,c00ffeff,c0107eef,c010fede
  //   ,c0117ecd,c011febb,c0127ea9,c012fe96,c0137e83,c013fe6f,c0147e5b
  //   ,c014fe46,c0157e31,c015fe1b,c0167e05,c016fdee,c0177dd7,c017fdbf
  //   ,c0187da7,c018fd8e,c0197d75,c019fd5b,c01a7d41,c01afd26,c01b7d0b
  //   ,c01bfcef,c01c7cd3,c01cfcb6,c01d7c99,c01dfc7b,c01e7c5d,c01efc3e
  //   ,c01f7c1f,c01ffbff,c0207bdf,c020fbbe,c0217b9d,c021fb7b,c0227b59
  //   ,c022fb36,c0237b13,c023faef,c0247acb,c024faa6,c0257a81,c025fa5b
  //   ,c0267a35,c026fa0e,c02779e7,c027f9bf,c0287997,c028f96e,c0297945
  //   ,c029f91b,c02a78f1,c02af8c6,c02b789b,c02bf86f,c02c7843,c02cf816
  //   ,c02d77e9,c02df7bb,c02e778d,c02ef75e,c02f772f,c02ff6ff,c03076cf
  //   ,c030f69e,c031766d,c031f63b,c0327609,c032f5d6,c03375a3,c033f56f
  //   ,c034753b,c034f506,c03574d1,c035f49b,c0367465,c036f42e,c03773f7
  //   ,c037f3bf,c0387387,c038f34e,c0397315,c039f2db,c03a72a1,c03af266
  //   ,c03b722b,c03bf1ef,c03c71b3,c03cf176,c03d7139,c03df0fb,c03e70bd
  //   ,c03ef07e,c03f703f,c03fefff,c0406fbf,c040ef7e,c0416f3d,c041eefb
  //   ,c0426eb9,c042ee76,c0436e33,c043edef,c0446dab,c044ed66,c0456d21
  //   ,c045ecdb,c0466c95,c046ec4e,c0476c07,c047ebbf,c0486b77,c048eb2e
  //   ,c0496ae5,c049ea9b,c04a6a51,c04aea06,c04b69bb,c04be96f,c04c6923
  //   ,c04ce8d6,c04d6889,c04de83b,c04e67ed,c04ee79e,c04f674f,c04fe6ff
  //   ,c05066af,c050e65e,c051660d,c051e5bb,c0526569,c052e516,c05364c3
  //   ,c053e46f,c054641b,c054e3c6,c0556371,c055e31b,c05662c5,c056e26e
  //   ,c0576217,c057e1bf,c0586167,c058e10e,c05960b5,c059e05b,c05a6001
  //   ,c05adfa6,c05b5f4b,c05bdeef,c05c5e93,c05cde36,c05d5dd9,c05ddd7b
  //   ,c05e5d1d,c05edcbe,c05f5c5f,c05fdbff,c0605b9f,c060db3e,c0615add
  //   ,c061da7b,c0625a19,c062d9b6,c0635953,c063d8ef,c064588b,c064d826
  //   ,c06557c1,c065d75b,c06656f5,c066d68e,c0675627,c067d5bf,c0685557
  //   ,c068d4ee,c0695485,c069d41b,c06a53b1,c06ad346,c06b52db,c06bd26f
  //   ,c06c5203,c06cd196,c06d5129,c06dd0bb,c06e504d,c06ecfde,c06f4f6f
  //   ,c06fceff,c0704e8f,c070ce1e,c0714dad,c071cd3b,c0724cc9,c072cc56
  //   ,c0734be3,c073cb6f,c0744afb,c074ca86,c0754a11,c075c99b,c0764925
  //   ,c076c8ae,c0774837,c077c7bf,c0784747,c078c6ce,c0794655,c079c5db
  //   ,c07a4561,c07ac4e6,c07b446b,c07bc3ef,c07c4373,c07cc2f6,c07d4279
  //   ,c07dc1fb,c07e417d,c07ec0fe,c07f407f,c07fbfff,c0803f7f,c080befe
  //   ,c0813e7d,c081bdfb,c0823d79,c082bcf6,c0833c73,c083bbef,c0843b6b
  //   ,c084bae6,c0853a61,c085b9db,c0863955,c086b8ce,c0873847,c087b7bf
  //   ,c0883737,c088b6ae,c0893625,c089b59b,c08a3511,c08ab486,c08b33fb
  //   ,c08bb36f,c08c32e3,c08cb256,c08d31c9,c08db13b,c08e30ad,c08eb01e
  //   ,c08f2f8f,c08faeff,c0902e6f,c090adde,c0912d4d,c091acbb,c0922c29
  //   ,c092ab96,c0932b03,c093aa6f,c09429db,c094a946,c09528b1,c095a81b
  //   ,c0962785,c096a6ee,c0972657,c097a5bf,c0982527,c098a48e,c09923f5
  //   ,c099a35b,c09a22c1,c09aa226,c09b218b,c09ba0ef,c09c2053,c09c9fb6
  //   ,c09d1f19,c09d9e7b,c09e1ddd,c09e9d3e,c09f1c9f,c09f9bff,c0a01b5f
  //   ,c0a09abe,c0a11a1d,c0a1997b,c0a218d9,c0a29836,c0a31793,c0a396ef
  //   ,c0a4164b,c0a495a6,c0a51501,c0a5945b,c0a613b5,c0a6930e,c0a71267
  //   ,c0a791bf,c0a81117,c0a8906e,c0a90fc5,c0a98f1b,c0aa0e71,c0aa8dc6
  //   ,c0ab0d1b,c0ab8c6f,c0ac0bc3,c0ac8b16,c0ad0a69,c0ad89bb,c0ae090d
  //   ,c0ae885e,c0af07af,c0af86ff,c0b0064f,c0b0859e,c0b104ed,c0b1843b
  //   ,c0b20389,c0b282d6,c0b30223,c0b3816f,c0b400bb,c0b48006,c0b4ff51
  //   ,c0b57e9b,c0b5fde5,c0b67d2e,c0b6fc77,c0b77bbf,c0b7fb07,c0b87a4e
  //   ,c0b8f995,c0b978db,c0b9f821,c0ba7766,c0baf6ab,c0bb75ef,c0bbf533
  //   ,c0bc7476,c0bcf3b9,c0bd72fb,c0bdf23d,c0be717e,c0bef0bf,c0bf6fff
  //   ,c0bfef3f,c0c06e7e,c0c0edbd,c0c16cfb,c0c1ec39,c0c26b76,c0c2eab3
  //   ,c0c369ef,c0c3e92b,c0c46866,c0c4e7a1,c0c566db,c0c5e615,c0c6654e
  //   ,c0c6e487,c0c763bf,c0c7e2f7,c0c8622e,c0c8e165,c0c9609b,c0c9dfd1
  //   ,c0ca5f06,c0cade3b,c0cb5d6f,c0cbdca3,c0cc5bd6,c0ccdb09,c0cd5a3b
  //   ,c0cdd96d,c0ce589e,c0ced7cf,c0cf56ff,c0cfd62f,c0d0555e,c0d0d48d
  //   ,c0d153bb,c0d1d2e9,c0d25216,c0d2d143,c0d3506f,c0d3cf9b,c0d44ec6
  //   ,c0d4cdf1,c0d54d1b,c0d5cc45,c0d64b6e,c0d6ca97,c0d749bf,c0d7c8e7
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endmodule
